// Logisim project MIPSpipeline.circ as structural Verilog: 2 circuits, main circuit main
module main (
  input  in_1
);

  wire CLK;
  wire [4:0] rom_1_p4;
  wire [7:0] rom_1_p2, rom_1_p3;
  wire [10:0] rom_1_p5;
  wire [19:0] adder_1_out, register_1_q;

  Register #(.width(20)) register_1 (.D(adder_1_out), .en(in_1), .clk(CLK), .Q(register_1_q));  // open: clr
  Clock clock_1 (.out(CLK));
  Adder #(.width(20)) adder_1 (.a(20'h4), .b(register_1_q), .out(adder_1_out));  // open: cin, cout
  // ROM #(.addrWidth(20), .line("quad")) rom_1: pin names not known; wires that end beside it: register_1_q, rom_1_p2, rom_1_p3, {rom_1_p4, rom_1_p5[10:8]}, rom_1_p5[7:0]
  registers registers_1 ();  // open: rs, data, rt, writeEnable, rd, A, B

  // Other names for the same wires on the sheet: PCwrite = in_1

  // Notes on the sheet:
  //   in_1: initial=0x1
  //   contents of rom_1 (hex, n*v repeats v):
  //   ff af fa b5 12 24 b4 31 12 45 21 2 16 63 61 a9 16 63 61 a9 16 63 61 a9 16 63 61 a9 16 63 61 a9
endmodule

module registers (
  input  [4:0] rs,
  input  [31:0] data,
  input  [4:0] rt,
  input  writeEnable,
  input  [4:0] rd,
  output [31:0] A,
  output [31:0] B
);

  wire CLK_out, demultiplexer_1_out1, demultiplexer_1_out2, demultiplexer_1_out3, demultiplexer_1_out4,
       demultiplexer_1_out5, demultiplexer_1_out6, demultiplexer_1_out7, demultiplexer_1_out8,
       demultiplexer_1_out9, demultiplexer_1_out10, demultiplexer_1_out11, demultiplexer_1_out12,
       demultiplexer_1_out13, demultiplexer_1_out14, demultiplexer_1_out15, demultiplexer_1_out16,
       demultiplexer_1_out17, demultiplexer_1_out18, demultiplexer_1_out19, demultiplexer_1_out20,
       demultiplexer_1_out21, demultiplexer_1_out22, demultiplexer_1_out23, demultiplexer_1_out24,
       demultiplexer_1_out25, demultiplexer_1_out26, demultiplexer_1_out27, demultiplexer_1_out28,
       demultiplexer_1_out29, demultiplexer_1_out30, demultiplexer_1_out31;
  wire [31:0] register_1_q, register_2_q, register_3_q, register_4_q, register_5_q, register_6_q,
       register_7_q, register_8_q, register_9_q, register_10_q, register_11_q, register_12_q, register_13_q,
       register_14_q, register_15_q, register_16_q, register_17_q, register_18_q, register_19_q,
       register_20_q, register_21_q, register_22_q, register_23_q, register_24_q, register_25_q,
       register_26_q, register_27_q, register_28_q, register_29_q, register_30_q, register_31_q,
       register_32_q;

  Demultiplexer #(.select(5)) demultiplexer_1 (
    .out1(demultiplexer_1_out1), .out2(demultiplexer_1_out2), .out3(demultiplexer_1_out3),
    .out4(demultiplexer_1_out4), .out5(demultiplexer_1_out5), .out6(demultiplexer_1_out6),
    .out7(demultiplexer_1_out7), .out8(demultiplexer_1_out8), .out9(demultiplexer_1_out9),
    .out10(demultiplexer_1_out10), .out11(demultiplexer_1_out11), .out12(demultiplexer_1_out12),
    .out13(demultiplexer_1_out13), .out14(demultiplexer_1_out14), .out15(demultiplexer_1_out15),
    .out16(demultiplexer_1_out16), .out17(demultiplexer_1_out17), .out18(demultiplexer_1_out18),
    .out19(demultiplexer_1_out19), .out20(demultiplexer_1_out20), .out21(demultiplexer_1_out21),
    .out22(demultiplexer_1_out22), .out23(demultiplexer_1_out23), .out24(demultiplexer_1_out24),
    .out25(demultiplexer_1_out25), .out26(demultiplexer_1_out26), .out27(demultiplexer_1_out27),
    .out28(demultiplexer_1_out28), .out29(demultiplexer_1_out29), .out30(demultiplexer_1_out30),
    .out31(demultiplexer_1_out31), .in(writeEnable), .sel(rd));  // open: out0
  Clock CLK (.out(CLK_out));
  Register #(.width(32)) register_1 (.D(data), .en(1'b0), .clk(CLK_out), .Q(register_1_q));  // open: clr
  Register #(.width(32)) register_2 (
    .D(data), .en(demultiplexer_1_out1), .clk(CLK_out), .Q(register_2_q));  // open: clr
  Register #(.width(32)) register_3 (
    .D(data), .en(demultiplexer_1_out2), .clk(CLK_out), .Q(register_3_q));  // open: clr
  Register #(.width(32)) register_4 (
    .D(data), .en(demultiplexer_1_out3), .clk(CLK_out), .Q(register_4_q));  // open: clr
  Register #(.width(32)) register_5 (
    .D(data), .en(demultiplexer_1_out4), .clk(CLK_out), .Q(register_5_q));  // open: clr
  Register #(.width(32)) register_6 (
    .D(data), .en(demultiplexer_1_out5), .clk(CLK_out), .Q(register_6_q));  // open: clr
  Register #(.width(32)) register_7 (
    .D(data), .en(demultiplexer_1_out6), .clk(CLK_out), .Q(register_7_q));  // open: clr
  Register #(.width(32)) register_8 (
    .D(data), .en(demultiplexer_1_out7), .clk(CLK_out), .Q(register_8_q));  // open: clr
  Register #(.width(32)) register_9 (
    .D(data), .en(demultiplexer_1_out8), .clk(CLK_out), .Q(register_9_q));  // open: clr
  Register #(.width(32)) register_10 (
    .D(data), .en(demultiplexer_1_out9), .clk(CLK_out), .Q(register_10_q));  // open: clr
  Register #(.width(32)) register_11 (
    .D(data), .en(demultiplexer_1_out10), .clk(CLK_out), .Q(register_11_q));  // open: clr
  Register #(.width(32)) register_12 (
    .D(data), .en(demultiplexer_1_out11), .clk(CLK_out), .Q(register_12_q));  // open: clr
  Register #(.width(32)) register_13 (
    .D(data), .en(demultiplexer_1_out12), .clk(CLK_out), .Q(register_13_q));  // open: clr
  Register #(.width(32)) register_14 (
    .D(data), .en(demultiplexer_1_out13), .clk(CLK_out), .Q(register_14_q));  // open: clr
  Register #(.width(32)) register_15 (
    .D(data), .en(demultiplexer_1_out14), .clk(CLK_out), .Q(register_15_q));  // open: clr
  Register #(.width(32)) register_16 (
    .D(data), .en(demultiplexer_1_out15), .clk(CLK_out), .Q(register_16_q));  // open: clr
  Register #(.width(32)) register_17 (
    .D(data), .en(demultiplexer_1_out16), .clk(CLK_out), .Q(register_17_q));  // open: clr
  Register #(.width(32)) register_18 (
    .D(data), .en(demultiplexer_1_out17), .clk(CLK_out), .Q(register_18_q));  // open: clr
  Register #(.width(32)) register_19 (
    .D(data), .en(demultiplexer_1_out18), .clk(CLK_out), .Q(register_19_q));  // open: clr
  Register #(.width(32)) register_20 (
    .D(data), .en(demultiplexer_1_out19), .clk(CLK_out), .Q(register_20_q));  // open: clr
  Register #(.width(32)) register_21 (
    .D(data), .en(demultiplexer_1_out20), .clk(CLK_out), .Q(register_21_q));  // open: clr
  Register #(.width(32)) register_22 (
    .D(data), .en(demultiplexer_1_out21), .clk(CLK_out), .Q(register_22_q));  // open: clr
  Register #(.width(32)) register_23 (
    .D(data), .en(demultiplexer_1_out22), .clk(CLK_out), .Q(register_23_q));  // open: clr
  Register #(.width(32)) register_24 (
    .D(data), .en(demultiplexer_1_out23), .clk(CLK_out), .Q(register_24_q));  // open: clr
  Register #(.width(32)) register_25 (
    .D(data), .en(demultiplexer_1_out24), .clk(CLK_out), .Q(register_25_q));  // open: clr
  Register #(.width(32)) register_26 (
    .D(data), .en(demultiplexer_1_out25), .clk(CLK_out), .Q(register_26_q));  // open: clr
  Register #(.width(32)) register_27 (
    .D(data), .en(demultiplexer_1_out26), .clk(CLK_out), .Q(register_27_q));  // open: clr
  Register #(.width(32)) register_28 (
    .D(data), .en(demultiplexer_1_out27), .clk(CLK_out), .Q(register_28_q));  // open: clr
  Register #(.width(32)) register_29 (
    .D(data), .en(demultiplexer_1_out28), .clk(CLK_out), .Q(register_29_q));  // open: clr
  Register #(.width(32)) register_30 (
    .D(data), .en(demultiplexer_1_out29), .clk(CLK_out), .Q(register_30_q));  // open: clr
  Register #(.width(32)) register_31 (
    .D(data), .en(demultiplexer_1_out30), .clk(CLK_out), .Q(register_31_q));  // open: clr
  Register #(.width(32)) register_32 (
    .D(data), .en(demultiplexer_1_out31), .clk(CLK_out), .Q(register_32_q));  // open: clr
  Multiplexer #(.select(5), .width(32)) multiplexer_1 (
    .in0(register_1_q), .in1(register_2_q), .in2(register_3_q), .in3(register_4_q), .in4(register_5_q),
    .in5(register_6_q), .in6(register_7_q), .in7(register_8_q), .in8(register_9_q), .in9(register_10_q),
    .in10(register_11_q), .in11(register_12_q), .in12(register_13_q), .in13(register_14_q),
    .in14(register_15_q), .in15(register_16_q), .in16(register_17_q), .in17(register_18_q),
    .in18(register_19_q), .in19(register_20_q), .in20(register_21_q), .in21(register_22_q),
    .in22(register_23_q), .in23(register_24_q), .in24(register_25_q), .in25(register_26_q),
    .in26(register_27_q), .in27(register_28_q), .in28(register_29_q), .in29(register_30_q),
    .in30(register_31_q), .in31(register_32_q), .out(A), .sel(rs));
  Multiplexer #(.select(5), .width(32)) multiplexer_2 (
    .in0(register_1_q), .in1(register_2_q), .in2(register_3_q), .in3(register_4_q), .in4(register_5_q),
    .in5(register_6_q), .in6(register_7_q), .in7(register_8_q), .in8(register_9_q), .in9(register_10_q),
    .in10(register_11_q), .in11(register_12_q), .in12(register_13_q), .in13(register_14_q),
    .in14(register_15_q), .in15(register_16_q), .in16(register_17_q), .in17(register_18_q),
    .in18(register_19_q), .in19(register_20_q), .in20(register_21_q), .in21(register_22_q),
    .in22(register_23_q), .in23(register_24_q), .in24(register_25_q), .in25(register_26_q),
    .in26(register_27_q), .in27(register_28_q), .in28(register_29_q), .in29(register_30_q),
    .in30(register_31_q), .in31(register_32_q), .out(B), .sel(rt));
endmodule
